# Fritzing sketch Bees (saved by Fritzing 0.9.2b)

parts:
  WeMos_D1_Mini1 = WeMos D1 Mini
  U1 = 74HC4052 [package=dil16]
  DHT1 = DHT22 Humidity and Temperature Sensor
  R1 = Resistor [tolerance=±5% resistance=1k package=THT]
  R2 = Resistor [tolerance=±5% resistance=1k package=THT]
  R3 = Resistor [tolerance=±5% resistance=220 package=THT]
  S1 = Pushbutton [package=THT]

nets:
  5V: WeMos_D1_Mini1.5V, U1.VCC, DHT1.VDD, R1.Pin_1, R2.Pin_1, S1.leg1
  N1: WeMos_D1_Mini1.A0, U1.X
  N2: WeMos_D1_Mini1.D1, DHT1.NULL, R2.Pin_0
  N3: WeMos_D1_Mini1.D2, DHT1.GND, R1.Pin_0
  N4: WeMos_D1_Mini1.D6, R3.Pin_1, S1.leg0
  N5: WeMos_D1_Mini1.D7, U1.B
  N6: WeMos_D1_Mini1.D8, U1.A
  N7: WeMos_D1_Mini1.G, U1.INH, U1.GND, DHT1.DATA, R3.Pin_0

custom parts:
  WeMos D1 Mini: The D1 mini is a mini wifi board based on ESP-8266EX.
